# Fritzing sketch ComptageBinaire (saved by Fritzing 0.9.3b)
breadboards: 1

parts:
  Raspberry_Pi_1 = Raspberry Pi 3 [part_number=RPI-3-V1.2]
  R1 = Resistor [tolerance=±5% resistance=220 package=THT]
  R2 = Resistor [tolerance=±5% resistance=220 package=THT]
  R3 = Resistor [tolerance=±5% resistance=220 package=THT]
  R4 = Resistor [tolerance=±5% resistance=220 package=THT]
  LED1 = LED - 5mm [color="Red (635nm)" package="5 mm [THT]"]
  LED2 = LED - 5mm [color="Red (635nm)" package="5 mm [THT]"]
  LED3 = LED - 5mm [color="Red (635nm)" package="5 mm [THT]"]
  LED4 = LED - 5mm [color="Red (635nm)" package="5 mm [THT]"]

nets:
  N1: Raspberry_Pi_1.GPIO2, R1.Pin_0
  N2: Raspberry_Pi_1.GPIO3, R2.Pin_0
  N3: Raspberry_Pi_1.GIPO4, R3.Pin_0
  N4: Raspberry_Pi_1.GND, LED1.cathode, LED2.cathode, LED3.cathode, LED4.cathode
  N5: Raspberry_Pi_1.GIPO5, R4.Pin_0
  N6: R1.Pin_1, LED1.anode
  N7: R2.Pin_1, LED2.anode
  N8: R3.Pin_1, LED3.anode
  N9: R4.Pin_1, LED4.anode
